# Fritzing sketch aquarium (saved by Fritzing 0.9.3b)
circuit board: 8.46667cm x 5.64444cm
breadboards: 1

parts:
  WeMos_D1_Mini1 = WeMos D1 Mini
  U1 = FS1000A - 433Mhz RF Transmitter [package=THT]
  2_Channel_Relay1 = 2 Channel Power Relay

nets:
  5V: WeMos_D1_Mini1.5V, U1.VCC, 2_Channel_Relay1.VCC#14
  N1: WeMos_D1_Mini1.D2, 2_Channel_Relay1.IN2
  N2: WeMos_D1_Mini1.D3, 2_Channel_Relay1.IN1
  N3: WeMos_D1_Mini1.D4, U1.DATA
  N4: WeMos_D1_Mini1.G, U1.GND, 2_Channel_Relay1.GND#11

custom parts:
  FS1000A - 433Mhz RF Transmitter: This is 433Mhz RF transmitter with receiver kit for Arduino ARM MCU wireless Application environment: Remote control switch, receiver module, motorcycles, automobile anti-theft products, home security products, electric doors, shutter doors, windows, remote control socket, remote control LED, remote audio remote control electric doors, garage door remote control, remote control retractable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
  2 Channel Power Relay: A 2 channel power relay. The module operates at 5V.
